// Digital circuit Heintz_Bb.dig as structural Verilog
module Heintz_Bb (
  input  C,
  input  A,
  input  B,
  output Y_1,
  output Y_0
);

  wire relaydt_1_p3, relaydt_2_p6, relaydt_2_p9;

  // RelayDT #(.relayNormallyClosed("true")) relaydt_1: pin names not known; wires that end beside it: C, 1'b1, relaydt_1_p3, relaydt_1_p3
  // RelayDT relaydt_2: pin names not known; wires that end beside it: 1'b0, Y_1, A, 1'b0, Y_1, relaydt_2_p6, relaydt_2_p6, Y_0, relaydt_2_p9
  // RelayDT #(.relayNormallyClosed("true")) relaydt_3: pin names not known; wires that end beside it: B, 1'b0, Y_0, relaydt_2_p9, Y_1
endmodule

/* Test case:
A B C Y_0 Y_1
0 0 0  z   z
0 0 1  1   1
0 1 0  z   z
0 1 1  1   1
1 0 0  z   z
1 0 1  z   1
1 1 0  z   z
1 1 1  1   1

# transitions
0 0 0 Z Z
0 0 1 1 1
0 0 0 Z Z
0 1 0 Z Z
0 0 0 Z Z
0 1 1 1 1
0 0 0 Z Z
1 0 0 Z Z
0 0 0 Z Z
1 0 1 Z 1
0 0 0 Z Z
1 1 0 Z Z
0 0 0 Z Z
1 1 1 1 1
0 0 0 Z Z
0 0 1 1 1
0 1 0 Z Z
0 0 1 1 1
0 1 1 1 1
0 0 1 1 1
1 0 0 Z Z
0 0 1 1 1
1 0 1 Z 1
0 0 1 1 1
1 1 0 Z Z
0 0 1 1 1
1 1 1 1 1
0 0 1 1 1
0 1 0 Z Z
0 1 1 1 1
0 1 0 Z Z
1 0 0 Z Z
0 1 0 Z Z
1 0 1 Z 1
0 1 0 Z Z
1 1 0 Z Z
0 1 0 Z Z
1 1 1 1 1
0 1 0 Z Z
0 1 1 1 1
1 0 0 Z Z
0 1 1 1 1
1 0 1 Z 1
0 1 1 1 1
1 1 0 Z Z
0 1 1 1 1
1 1 1 1 1
0 1 1 1 1
1 0 0 Z Z
1 0 1 Z 1
1 0 0 Z Z
1 1 0 Z Z
1 0 0 Z Z
1 1 1 1 1
1 0 0 Z Z
1 0 1 Z 1
1 1 0 Z Z
1 0 1 Z 1
1 1 1 1 1
1 0 1 Z 1
1 1 0 Z Z
1 1 1 1 1
1 1 0 Z Z
*/
