// Digital circuit burn1.dig as structural Verilog
module burn1 (
  input  A,
  output Y
);

  wire relaydt_1_p3;

  // RelayDT relaydt_1: pin names not known; wires that end beside it: A, 1'b0, relaydt_1_p3, relaydt_1_p3, 1'b1, 1'b0

  assign Y = 1'b1;
endmodule

/* Test case Failing:
A Y
1 1
*/
