// Digital circuit burn1b.dig as structural Verilog
module burn1b (
  input  A,
  output Y
);

  wire relaydt_1_p4;

  // RelayDT #(.relayNormallyClosed("true")) relaydt_1: pin names not known; wires that end beside it: A, 1'b0, 1'b1, relaydt_1_p4, 1'b0, relaydt_1_p4

  assign Y = 1'b1;
endmodule

/* Test case Failing:
A Y
1 1
*/
