// Digital circuit burn2.dig as structural Verilog
module burn2 (
  input  A,
  output Y
);

  wire pullup_1_out, relaydt_1_p3, relaydt_1_p6;

  PullUp pullup_1 (.out(pullup_1_out));
  // RelayDT relaydt_1: pin names not known; wires that end beside it: A, 1'b0, relaydt_1_p3, relaydt_1_p3, pullup_1_out, relaydt_1_p6
  PullDown pulldown_1 (.out(relaydt_1_p6));

  assign Y = 1'b1;
endmodule

/* Test case Failing:
A Y
1 1
*/
