// Digital circuit burn2b.dig as structural Verilog
module burn2b (
  input  A,
  output Y
);

  wire pullup_1_out, relaydt_1_p4, relaydt_1_p5;

  PullUp pullup_1 (.out(pullup_1_out));
  // RelayDT #(.relayNormallyClosed("true")) relaydt_1: pin names not known; wires that end beside it: A, 1'b0, pullup_1_out, relaydt_1_p4, relaydt_1_p5, relaydt_1_p4
  PullDown pulldown_1 (.out(relaydt_1_p5));

  assign Y = 1'b1;
endmodule

/* Test case Failing:
A Y
1 1
*/
