// Digital circuit inverter1.dig as structural Verilog
module inverter1 (
  input  A,
  output Y
);

  wire relaydt_1_p4, relaydt_1_p6;

  // RelayDT #(.relayNormallyClosed("true")) relaydt_1: pin names not known; wires that end beside it: A, 1'b0, A, relaydt_1_p4, relaydt_1_p4, relaydt_1_p6, relaydt_1_p6, 1'b1, Y, Y
  // RelayDT relaydt_2: pin names not known; wires that end beside it: 1'b0, 1'b0
endmodule

/* Test case:
A Y
0 1
1 0
z 1


# transitions
0 1
1 0
0 1
Z 1
0 1
1 0
Z 1
1 0
*/
