// Digital circuit inverter1b.dig as structural Verilog
module inverter1b (
  input  A,
  output Y
);

  wire relaydt_1_p6, relaydt_1_p9;

  // RelayDT relaydt_1: pin names not known; wires that end beside it: A, 1'b0, A, 1'b1, Y, relaydt_1_p6, relaydt_1_p6, Y, relaydt_1_p9, relaydt_1_p9
  // RelayDT #(.relayNormallyClosed("true")) relaydt_2: pin names not known; wires that end beside it: 1'b0, 1'b0
endmodule

/* Test case:
A Y
0 1
1 0
z 1


# transitions
0 1
1 0
0 1
Z 1
0 1
1 0
Z 1
1 0
*/
