// Digital circuit inverter2.dig as structural Verilog
module inverter2 (
  input  A,
  output Y
);

  // RelayDT relaydt_1: pin names not known; wires that end beside it: 1'b0, 1'b1, A, Y, 1'b0
endmodule

/* Test case:
A Y
0 1
1 0
z 1


# transitions
0 1
1 0
0 1
Z 1
0 1
1 0
Z 1
1 0
*/
