// Digital circuit inverter2b.dig as structural Verilog
module inverter2b (
  input  A,
  output Y
);

  // RelayDT #(.relayNormallyClosed("true")) relaydt_1: pin names not known; wires that end beside it: 1'b1, 1'b0, A, Y, 1'b0
endmodule

/* Test case:
A Y
0 1
1 0
z 1


# transitions
0 1
1 0
0 1
Z 1
0 1
1 0
Z 1
1 0
*/
