// Digital circuit latch.dig as structural Verilog
module latch (
  input  O,
  input  C,
  output Y,
  output Center
);

  wire relaydt_1_p3, relaydt_1_p5, relaydt_3_p3;

  // RelayDT #(.relayNormallyClosed("true")) relaydt_1: pin names not known; wires that end beside it: O, 1'b0, relaydt_1_p3, relaydt_1_p3, relaydt_1_p5, 1'b1, Center
  // RelayDT relaydt_2: pin names not known; wires that end beside it: C, 1'b0, relaydt_1_p5, Center, Y
  // RelayDT relaydt_3: pin names not known; wires that end beside it: 1'b0, Y, relaydt_3_p3, relaydt_3_p3, Center, Y
  PullDown pulldown_1 (.out(Y));
endmodule

/* Test case:
O C Y Center
0 0 0 1
0 1 1 1
0 0 1 1
1 0 0 z
1 1 0 0
0 1 1 1
*/
