// Digital circuit latchb.dig as structural Verilog
module latchb (
  input  O,
  input  C,
  output Y,
  output Center
);

  wire relaydt_1_p4, relaydt_1_p7, relaydt_3_p4;

  // RelayDT relaydt_1: pin names not known; wires that end beside it: O, 1'b0, 1'b1, relaydt_1_p4, relaydt_1_p4, Center, relaydt_1_p7
  // RelayDT #(.relayNormallyClosed("true")) relaydt_2: pin names not known; wires that end beside it: C, 1'b0, Center, relaydt_1_p7, Y
  // RelayDT #(.relayNormallyClosed("true")) relaydt_3: pin names not known; wires that end beside it: 1'b0, Y, Center, relaydt_3_p4, relaydt_3_p4, Y
  PullDown pulldown_1 (.out(Y));
endmodule

/* Test case:
O C Y Center
0 0 0 1
0 1 1 1
0 0 1 1
1 0 0 z
1 1 0 0
0 1 1 1
*/
