// Digital circuit no_net.dig as structural Verilog
module no_net (
  input  O,
  output Y
);

  wire relaydt_1_p3;

  // RelayDT relaydt_1: pin names not known; wires that end beside it: O, 1'b0, relaydt_1_p3, relaydt_1_p3, 1'b1, Y
endmodule

/* Test case:
O Y
0 z
1 1
*/
