// Digital circuit no_netb.dig as structural Verilog
module no_netb (
  input  O,
  output Y
);

  wire relaydt_1_p4;

  // RelayDT #(.relayNormallyClosed("true")) relaydt_1: pin names not known; wires that end beside it: O, 1'b0, 1'b1, relaydt_1_p4, relaydt_1_p4, Y
endmodule

/* Test case:
O Y
0 z
1 1
*/
