// Digital circuit switch1.dig as structural Verilog
module switch1 (
  input  A,
  input  B,
  input  C,
  output Y
);

  wire relaydt_1_p4, relaydt_1_p5, relaydt_2_p5, relaydt_2_p8;

  // RelayDT relaydt_1: pin names not known; wires that end beside it: A, 1'b1, 1'b0, relaydt_1_p4, relaydt_1_p5, relaydt_1_p4
  // RelayDT relaydt_2: pin names not known; wires that end beside it: C, relaydt_1_p5, B, 1'b0, relaydt_2_p5, Y, 1'b0, relaydt_2_p8, relaydt_2_p5, relaydt_2_p8
  // RelayDT relaydt_3: pin names not known; wires that end beside it: relaydt_1_p5, Y
endmodule

/* Test case:
A B C Y
0 0 0 Z
0 0 1 Z
0 1 0 Z
0 1 1 Z
1 0 0 Z
1 0 1 1
1 1 0 1
1 1 1 1

# transitions
0 0 0 Z
0 0 1 Z
0 0 0 Z
0 1 0 Z
0 0 0 Z
0 1 1 Z
0 0 0 Z
1 0 0 Z
0 0 0 Z
1 0 1 1
0 0 0 Z
1 1 0 1
0 0 0 Z
1 1 1 1
0 0 0 Z
0 0 1 Z
0 1 0 Z
0 0 1 Z
0 1 1 Z
0 0 1 Z
1 0 0 Z
0 0 1 Z
1 0 1 1
0 0 1 Z
1 1 0 1
0 0 1 Z
1 1 1 1
0 0 1 Z
0 1 0 Z
0 1 1 Z
0 1 0 Z
1 0 0 Z
0 1 0 Z
1 0 1 1
0 1 0 Z
1 1 0 1
0 1 0 Z
1 1 1 1
0 1 0 Z
0 1 1 Z
1 0 0 Z
0 1 1 Z
1 0 1 1
0 1 1 Z
1 1 0 1
0 1 1 Z
1 1 1 1
0 1 1 Z
1 0 0 Z
1 0 1 1
1 0 0 Z
1 1 0 1
1 0 0 Z
1 1 1 1
1 0 0 Z
1 0 1 1
1 1 0 1
1 0 1 1
1 1 1 1
1 0 1 1
1 1 0 1
1 1 1 1
1 1 0 1
*/
