// Digital circuit switch1b.dig as structural Verilog
module switch1b (
  input  A,
  input  B,
  input  C,
  output Y
);

  wire relaydt_1_p4, relaydt_1_p5, relaydt_2_p6, relaydt_3_p2;

  // RelayDT #(.relayNormallyClosed("true")) relaydt_1: pin names not known; wires that end beside it: A, 1'b1, 1'b0, relaydt_1_p4, relaydt_1_p5, relaydt_1_p5
  // RelayDT #(.relayNormallyClosed("true")) relaydt_2: pin names not known; wires that end beside it: C, relaydt_1_p4, B, 1'b0, Y, relaydt_2_p6, 1'b0, Y, relaydt_2_p6
  // RelayDT #(.relayNormallyClosed("true")) relaydt_3: pin names not known; wires that end beside it: relaydt_1_p4, relaydt_3_p2, relaydt_3_p2
endmodule

/* Test case:
A B C Y
0 0 0 Z
0 0 1 Z
0 1 0 Z
0 1 1 Z
1 0 0 Z
1 0 1 1
1 1 0 1
1 1 1 1

# transitions
0 0 0 Z
0 0 1 Z
0 0 0 Z
0 1 0 Z
0 0 0 Z
0 1 1 Z
0 0 0 Z
1 0 0 Z
0 0 0 Z
1 0 1 1
0 0 0 Z
1 1 0 1
0 0 0 Z
1 1 1 1
0 0 0 Z
0 0 1 Z
0 1 0 Z
0 0 1 Z
0 1 1 Z
0 0 1 Z
1 0 0 Z
0 0 1 Z
1 0 1 1
0 0 1 Z
1 1 0 1
0 0 1 Z
1 1 1 1
0 0 1 Z
0 1 0 Z
0 1 1 Z
0 1 0 Z
1 0 0 Z
0 1 0 Z
1 0 1 1
0 1 0 Z
1 1 0 1
0 1 0 Z
1 1 1 1
0 1 0 Z
0 1 1 Z
1 0 0 Z
0 1 1 Z
1 0 1 1
0 1 1 Z
1 1 0 1
0 1 1 Z
1 1 1 1
0 1 1 Z
1 0 0 Z
1 0 1 1
1 0 0 Z
1 1 0 1
1 0 0 Z
1 1 1 1
1 0 0 Z
1 0 1 1
1 1 0 1
1 0 1 1
1 1 1 1
1 0 1 1
1 1 0 1
1 1 1 1
1 1 0 1
*/
