// Digital circuit switch2b.dig as structural Verilog
module switch2b (
  input  A,
  input  [7:0] B,
  output [7:0] Y
);

  wire relaydt_1_p5;

  // RelayDT #(.Bits(8), .relayNormallyClosed("true")) relaydt_1: pin names not known; wires that end beside it: A, B, 1'b0, Y, relaydt_1_p5, relaydt_1_p5
endmodule

/* Test case:
A B Y
0 0 z 
0 7 z 
1 0 0 
1 7 7 
*/
