// Digital circuit switch2c.dig as structural Verilog
module switch2c (
  input  A,
  input  [7:0] B,
  output [7:0] Y
);

  wire relaydt_1_p4;

  // RelayDT #(.Bits(8)) relaydt_1: pin names not known; wires that end beside it: A, Y, 1'b0, relaydt_1_p4, B, relaydt_1_p4
endmodule

/* Test case:
A B Y
0 0 z 
0 7 z 
1 0 0 
1 7 7 
*/
