// Digital circuit switch_highZ.dig as structural Verilog
module switch_highZ (
  input  A,
  input  B,
  output a_2,
  output b_2
);

  wire relaydt_1_p3, relaydt_2_p3;

  // RelayDT relaydt_1: pin names not known; wires that end beside it: A, 1'b0, relaydt_1_p3, relaydt_1_p3, 1'b1, a_2
  // RelayDT #(.relayNormallyClosed("true")) relaydt_2: pin names not known; wires that end beside it: B, 1'b0, relaydt_2_p3, relaydt_2_p3, 1'b1, b_2
endmodule

/* Test case norm. open:
A a
0 z
1 1
z z
*/

/* Test case norm. closed:
B b
0 1
1 z
z 1
*/
