// Digital circuit switch_highZb.dig as structural Verilog
module switch_highZb (
  input  A,
  input  B,
  output a_2,
  output b_2
);

  wire relaydt_1_p4, relaydt_2_p4;

  // RelayDT #(.relayNormallyClosed("true")) relaydt_1: pin names not known; wires that end beside it: A, 1'b0, 1'b1, relaydt_1_p4, a_2, relaydt_1_p4
  // RelayDT relaydt_2: pin names not known; wires that end beside it: B, 1'b0, 1'b1, relaydt_2_p4, b_2, relaydt_2_p4
endmodule

/* Test case norm. closed:
A a
0 z
1 1
z z
*/

/* Test case norm. open:
B b
0 1
1 z
z 1
*/
