// Digital circuit switch_simple.dig as structural Verilog
module switch_simple (
  input  A,
  output Y1,
  output Y2,
  output Y3,
  output Y4,
  output Y5,
  output Y6,
  output Y7,
  output Y8
);

  wire relaydt_1_p4, relaydt_1_p7, relaydt_2_p5, relaydt_3_p5, relaydt_5_p3, relaydt_6_p1, relaydt_7_p1,
       relaydt_8_p1;

  // RelayDT relaydt_1: pin names not known; wires that end beside it: A, 1'b0, A, relaydt_1_p4, Y1, 1'b0, relaydt_1_p7, relaydt_1_p7
  // RelayDT relaydt_2: pin names not known; wires that end beside it: 1'b0, A, Y2, 1'b0, relaydt_2_p5, relaydt_2_p5
  // RelayDT relaydt_3: pin names not known; wires that end beside it: 1'b1, A, Y3, 1'b0, relaydt_3_p5, relaydt_3_p5
  // RelayDT relaydt_4: pin names not known; wires that end beside it: 1'b1, Y4
  // RelayDT relaydt_5: pin names not known; wires that end beside it: 1'b0, relaydt_1_p4, relaydt_5_p3, 1'b0, relaydt_5_p3, A, Y5, 1'b0
  // RelayDT relaydt_6: pin names not known; wires that end beside it: relaydt_6_p1, 1'b0, relaydt_6_p1, A, Y6, 1'b0
  // RelayDT relaydt_7: pin names not known; wires that end beside it: relaydt_7_p1, 1'b1, relaydt_7_p1, A, Y7, 1'b0
  // RelayDT relaydt_8: pin names not known; wires that end beside it: relaydt_8_p1, 1'b1, relaydt_8_p1, A, Y8, 1'b0
endmodule

/* Test case:
A Y1 Y2 Y3 Y4 Y5 Y6 Y7 Y8
0 z  z  z  z  z  z  z  z
1 0  0  1  1  0  0  1  1
0 z  z  z  z  z  z  z  z
1 0  0  1  1  0  0  1  1
*/
