// Digital circuit switch_xor.dig as structural Verilog
module switch_xor (
  input  A,
  input  B,
  output Y
);

  wire relaydt_1_p3;

  // RelayDT relaydt_1: pin names not known; wires that end beside it: A, B, relaydt_1_p3, relaydt_1_p3, 1'b1, Y
  PullDown pulldown_1 (.out(Y));
endmodule

/* Test case:
A B Y
0 0 0
0 1 1
1 0 1
1 1 0


# transitions
0 0 0
0 1 1
0 0 0
1 0 1
0 0 0
1 1 0
0 0 0
0 1 1
1 0 1
0 1 1
1 1 0
0 1 1
1 0 1
1 1 0
1 0 1
*/
