// Digital circuit relayFullAdder2.dig as structural Verilog
module relayFullAdder2 (
  input  [1:0] A,
  input  [1:0] B,
  input  C_in,
  output C_out,
  output [1:0] S
);

  wire relaydt_1_p3, relaydt_1_p4, relaydt_1_p5, relaydt_2_p2, relaydt_2_p3, relaydt_2_p4, relaydt_3_p4,
       relaydt_3_p6, relaydt_3_p12, relaydt_3_p13, relaydt_4_p3, relaydt_4_p5, relaydt_4_p11, relaydt_5_p2,
       relaydt_5_p3, relaydt_5_p4, relaydt_6_p2, relaydt_6_p3, relaydt_6_p4, relaydt_7_p1, relaydt_7_p3,
       relaydt_8_p1, relaydt_8_p3;

  // RelayDT #(.poles(2), .relayNormallyClosed("true")) relaydt_1: pin names not known; wires that end beside it: 1'b1, A[1], relaydt_1_p3, relaydt_1_p4, relaydt_1_p5
  // RelayDT #(.poles(2), .relayNormallyClosed("true")) relaydt_2: pin names not known; wires that end beside it: 1'b1, relaydt_2_p2, relaydt_2_p3, relaydt_2_p4
  // RelayDT #(.poles(2), .relayNormallyClosed("true")) relaydt_3: pin names not known; wires that end beside it: A[0], 1'b1, 1'b0, relaydt_3_p4, relaydt_1_p4, relaydt_3_p6, relaydt_3_p4, relaydt_1_p3, relaydt_1_p5, relaydt_3_p6, B[0], relaydt_3_p12, relaydt_3_p13, 1'b0, relaydt_3_p12, 1'b1, 1'b0
  // RelayDT #(.poles(2), .relayNormallyClosed("true")) relaydt_4: pin names not known; wires that end beside it: 1'b1, 1'b0, relaydt_4_p3, relaydt_2_p3, relaydt_4_p5, relaydt_4_p3, relaydt_2_p2, relaydt_2_p4, relaydt_4_p5, B[1], relaydt_4_p11, C_out, 1'b0, relaydt_4_p11, 1'b1, 1'b0
  // RelayDT #(.poles(2), .relayNormallyClosed("true")) relaydt_5: pin names not known; wires that end beside it: 1'b1, relaydt_5_p2, relaydt_5_p3, relaydt_5_p4
  // RelayDT #(.poles(2), .relayNormallyClosed("true")) relaydt_6: pin names not known; wires that end beside it: 1'b1, relaydt_6_p2, relaydt_6_p3, relaydt_6_p4
  // RelayDT #(.poles(2), .relayNormallyClosed("true")) relaydt_7: pin names not known; wires that end beside it: relaydt_7_p1, relaydt_5_p3, relaydt_7_p3, relaydt_7_p1, relaydt_5_p2, relaydt_5_p4, relaydt_7_p3, C_in, S[0], relaydt_3_p13, 1'b0
  // RelayDT #(.poles(2), .relayNormallyClosed("true")) relaydt_8: pin names not known; wires that end beside it: relaydt_8_p1, relaydt_6_p3, relaydt_8_p3, relaydt_8_p1, relaydt_6_p2, relaydt_6_p4, relaydt_8_p3, relaydt_3_p13, S[1], C_out, 1'b0
  PullDown #(.Bits(2)) pulldown_1 (.out(S));
  PullDown pulldown_2 (.out(C_out));
endmodule

/* Test case:
A B C_in S C_out
loop (C,2)
loop (A,4)
loop (B,4)
let s=A+B+C;
 (A) (B) (C) (s&3) (s>>2)
end loop
end loop
end loop
*/
