// Digital circuit relayFullAdderZuse.dig as structural Verilog
// Konrad Zuse’s Full Adder Circuit.
// Invented for the Z3 computer built in 1941.
// Makes use of "floating zero" logic.
// i.e. levels are limited to high-z (for 0) and 1.
module relayFullAdderZuse (
  input  A,
  input  B,
  input  C_in,
  input  nC_in,
  output Sum,
  output C_out,
  output nC_out
);

  wire relaydt_1_p8, relaydt_1_p9, relaydt_1_p10, relaydt_1_p11, relaydt_1_p12, relaydt_1_p14;

  // RelayDT #(.poles(4)) relaydt_1: pin names not known; wires that end beside it: A, nC_in, Sum, 1'b1, C_in, B, 1'b0, relaydt_1_p8, relaydt_1_p9, relaydt_1_p10, relaydt_1_p11, relaydt_1_p12, relaydt_1_p8, relaydt_1_p14, relaydt_1_p12, 1'b0
  // RelayDT #(.poles(4)) relaydt_2: pin names not known; wires that end beside it: nC_out, nC_in, C_in, C_out, relaydt_1_p9, relaydt_1_p8, relaydt_1_p11, relaydt_1_p10, relaydt_1_p10, relaydt_1_p11, relaydt_1_p12, relaydt_1_p14
endmodule

/* Test case Konrad Zuse’s Full Adder Circuit:
A B C_in ~C_in Sum C_out ~C_out
Z Z Z 1  Z Z 1

Z Z 1 Z  1 Z 1
Z 1 Z 1  1 Z 1
1 Z Z 1  1 Z 1

Z 1 1 Z  Z 1 Z
1 1 Z 1  Z 1 Z
1 Z 1 Z  Z 1 Z

1 1 1 Z  1 1 Z
*/
